# Fritzing sketch Pinout (saved by Fritzing 0.9.3b)

parts:
  MCU1 = Raspberry Pi Zero
  Part1 = PowerBoost 500 Charger
  R1 = PHOTOCELL [package=photocell]
  R2 = Resistor [tolerance=±5% resistance=10k package=THT]
  LED1 = LEDs [package=led10mm]
  S1 = Toggle Switch [package=THT]
  Bat1 = battery_holder_single_18650
  R3 = Resistor [tolerance=±5% resistance=10k package=THT]

nets:
  N1: MCU1.pin_1, MCU1.pin_17, R2.Pin_0
  N2: MCU1.pin_2, MCU1.pin_4, Part1.5.0V, R3.Pin_0
  N3: MCU1.pin_6, MCU1.pin_9, MCU1.pin_14, MCU1.pin_34, Part1.GND, LED1.A, S1.L2, Bat1.+#0
  N4: MCU1.pin_11, R1.P$2
  N5: Part1.VBAT_OUT, Bat1.+#1
  N6: Part1.ENABLE, S1.COM
  N7: R1.P$1, R2.Pin_1
  N8: LED1.C, R3.Pin_1

custom parts:
  battery_holder_single_18650: single 18650 battery holder
