# Fritzing sketch Pinout (saved by Fritzing 0.9.3b)

parts:
  MCU1 = Raspberry Pi Zero
  Part1 = PowerBoost 500 Charger
  S1 = Toggle Switch [package=THT]
  Bat1 = battery_holder_single_18650

nets:
  N1: MCU1.pin_2, MCU1.pin_4, Part1.5.0V
  N2: MCU1.pin_6, MCU1.pin_9, MCU1.pin_34, Part1.GND, S1.L2, Bat1.+#0
  N3: Part1.VBAT_OUT, Bat1.+#1
  N4: Part1.ENABLE, S1.COM

custom parts:
  battery_holder_single_18650: single 18650 battery holder
